// Logisim project CPU.circ as structural Verilog: 5 circuits, main circuit main
module main (
);

  wire and_1_out, and_2_out, and_3_out, and_4_out, and_5_out, buffer_1_out, clock_1_out, comparator_1_eq,
       control_1_acc_write, control_1_alu_src, control_1_branch, control_1_cond_branch, control_1_out,
       control_1_ram, controlled_buffer_1_out, not_1_out, Off_out, On_out, or_1_out, pull_resistor_1_node,
       Reset_Acc_out, Reset_OUT_out, Reset_PC_out, Reset_RAM_out, s_r_ff_1_q, t_ff_1_q, t_ff_1_qn;
  wire [1:0] control_1_acc_dst, control_1_acc_src;
  wire [2:0] control_1_alu_op;
  wire [3:0] bitselector_2_out;
  wire [7:0] Acc_q, ALU_out, bitselector_1_out, demultiplexer_1_out0, demultiplexer_1_out1,
       demultiplexer_1_out3, multiplexer_1_out, multiplexer_2_out, OUT_q, PC_out, ram_1_data;
  wire [11:0] Pgm_Mem_data_out;

  Pull_Resistor pull_resistor_1 (.node(pull_resistor_1_node));
  Button On (.out(On_out));
  Button Off (.out(Off_out));
  Button Reset_Acc (.out(Reset_Acc_out));
  Button Reset_OUT (.out(Reset_OUT_out));
  Button Reset_RAM (.out(Reset_RAM_out));
  Button Reset_PC (.out(Reset_PC_out));
  S_R_Flip_Flop #(.trigger("low")) s_r_ff_1 (
    .S(On_out), .clk(pull_resistor_1_node), .R(Off_out), .Q(s_r_ff_1_q));  // open: Qn, preset, reset, en
  Clock clock_1 (.out(clock_1_out));
  assign controlled_buffer_1_out = s_r_ff_1_q ? clock_1_out : 1'bz;  // Controlled_Buffer controlled_buffer_1
  T_Flip_Flop t_ff_1 (
    .clk(controlled_buffer_1_out), .T(1'b1), .Q(t_ff_1_q), .Qn(t_ff_1_qn));  // open: preset, reset, en
  Register Acc (.D(multiplexer_1_out), .Q(Acc_q), .clk(and_1_out), .clr(Reset_Acc_out));  // open: en
  Multiplexer #(.select(2), .width(8), .enable("false")) multiplexer_1 (
    .in0(bitselector_1_out), .in1(ALU_out), .in2(ram_1_data), .out(multiplexer_1_out), .sel(control_1_acc_src));  // open: in3
  and and_1 (and_1_out, t_ff_1_q, control_1_acc_write);
  Demultiplexer #(.select(2), .width(8), .enable("false")) demultiplexer_1 (
    .out0(demultiplexer_1_out0), .out1(demultiplexer_1_out1), .out3(demultiplexer_1_out3), .in(Acc_q),
    .sel(control_1_acc_dst));  // open: out2
  Program_Counter PC (.Inc(t_ff_1_qn), .Reset(Reset_PC_out), .In(bitselector_1_out), .Set(and_2_out), .Out(PC_out));
  Program_Memory Pgm_Mem (.Addr(PC_out), .Fetch(buffer_1_out), .Data_Out(Pgm_Mem_data_out));  // open: Data_In, Write
  buf buffer_1 (buffer_1_out, t_ff_1_qn);
  and and_2 (and_2_out, t_ff_1_q, or_1_out);
  BitSelector #(.width(12), .group(8)) bitselector_1 (.in(Pgm_Mem_data_out), .out(bitselector_1_out), .sel(1'b0));
  BitSelector #(.width(12), .group(4)) bitselector_2 (.in(Pgm_Mem_data_out), .out(bitselector_2_out), .sel(2'b10));
  or or_1 (or_1_out, and_3_out, control_1_branch);
  and and_3 (and_3_out, comparator_1_eq, control_1_cond_branch);
  Comparator comparator_1 (.a(Acc_q), .b({8{1'b0}}), .eq(comparator_1_eq));  // open: gt, lt
  and and_4 (and_4_out, t_ff_1_q, not_1_out);
  Control control_1 (
    .OP(bitselector_2_out), .RAM(control_1_ram), .ALU_Src(control_1_alu_src), .ALU_OP(control_1_alu_op),
    .Out(control_1_out), .Acc_Src(control_1_acc_src), .Acc_Write(control_1_acc_write),
    .Acc_Dst(control_1_acc_dst), .Cond_Branch(control_1_cond_branch), .Branch(control_1_branch));
  RAM #(.bus("separate")) ram_1 (
    .addr(bitselector_1_out), .din(demultiplexer_1_out1), .data(ram_1_data), .str(not_1_out),
    .clk(and_4_out), .ld(control_1_ram), .clr(Reset_RAM_out));  // open: sel
  not not_1 (not_1_out, control_1_ram);
  Multiplexer #(.width(8), .enable("false")) multiplexer_2 (
    .in0(bitselector_1_out), .in1(ram_1_data), .out(multiplexer_2_out), .sel(control_1_alu_src));
  and and_5 (and_5_out, control_1_out, t_ff_1_q);
  ALU ALU (.In_A(demultiplexer_1_out0), .In_B(multiplexer_2_out), .Operation(control_1_alu_op), .Out(ALU_out));
  Hex_Digit_Display hex_digit_display_1 (.value(OUT_q[7:4]));  // open: dp
  Register OUT (.D(demultiplexer_1_out3), .Q(OUT_q), .clk(and_5_out), .clr(Reset_OUT_out));  // open: en
  Hex_Digit_Display hex_digit_display_2 (.value(OUT_q[3:0]));  // open: dp
  LED led_1 (.in(OUT_q[0]));
  LED led_2 (.in(OUT_q[1]));
  LED led_3 (.in(OUT_q[2]));
  LED led_4 (.in(OUT_q[3]));
  LED led_5 (.in(OUT_q[4]));
  LED led_6 (.in(OUT_q[5]));
  LED led_7 (.in(OUT_q[6]));
  LED led_8 (.in(OUT_q[7]));
endmodule

module Program_Counter (
  input  [7:0] In,
  input  Inc,
  input  Set,
  input  Reset,
  output [7:0] Out
);

  wire or_1_out;

  Counter counter_1 (.load(Set), .D(In), .count(Inc), .Q(Out), .clk(or_1_out), .clr(Reset));  // open: carry
  or or_1 (or_1_out, Inc, Set);

  // Notes on the sheet:
  //   In: pull=down
  //   Reset: pull=down
  //   Set: pull=down
  //   Inc: pull=down
endmodule

module Program_Memory (
  input  Write,
  input  [11:0] Data_In,
  input  [7:0] Addr,
  input  Fetch,
  output [11:0] Data_Out
);

  wire pull_resistor_1_node;
  wire [11:0] ram_1_data;

  RAM #(.dataWidth(12), .bus("separate")) ram_1 (
    .addr(Addr), .din(Data_In), .data(ram_1_data), .str(Write), .clk(Write), .ld(Fetch));  // open: sel, clr
  Register #(.width(12), .trigger("low")) register_1 (
    .D(ram_1_data), .Q(Data_Out), .clk(pull_resistor_1_node));  // open: en, clr
  Pull_Resistor pull_resistor_1 (.node(pull_resistor_1_node));

  // Notes on the sheet:
  //   Fetch: pull=down
  //   Write: pull=down
endmodule

module ALU (
  input  [7:0] In_A,
  input  [7:0] In_B,
  input  [2:0] Operation,
  output [7:0] Out
);

  wire [7:0] adder_1_out, and_1_out, not_1_out, or_1_out, subtractor_1_out;

  Adder adder_1 (.a(In_A), .b(In_B), .out(adder_1_out));  // open: cin, cout
  Subtractor subtractor_1 (.a(In_A), .b(In_B), .out(subtractor_1_out));  // open: bin, bout
  assign and_1_out = In_A & In_B;  // AND_Gate and_1, 8 bits wide
  assign or_1_out = In_A | In_B;  // OR_Gate or_1, 8 bits wide
  assign not_1_out = ~In_A;  // NOT_Gate not_1, 8 bits wide
  Multiplexer #(.select(3), .width(8), .enable("false")) multiplexer_1 (
    .in0(adder_1_out), .in1(subtractor_1_out), .in2(and_1_out), .in3(or_1_out), .in4(not_1_out), .out(Out),
    .sel(Operation));  // open: in5, in6, in7
endmodule

// CTRL
module Control (
  input  [3:0] OP,
  output RAM,
  output ALU_Src,
  output [2:0] ALU_OP,
  output Out,
  output [1:0] Acc_Src,
  output Acc_Write,
  output [1:0] Acc_Dst,
  output Cond_Branch,
  output Branch
);

  ROM #(.addrWidth(4), .dataWidth(1)) rom_1 (.addr(OP), .data(RAM));  // open: sel
  ROM #(.addrWidth(4), .dataWidth(1)) rom_2 (.addr(OP), .data(ALU_Src));  // open: sel
  ROM #(.addrWidth(4), .dataWidth(3)) rom_3 (.addr(OP), .data(ALU_OP));  // open: sel
  ROM #(.addrWidth(4), .dataWidth(1)) rom_4 (.addr(OP), .data(Out));  // open: sel
  ROM #(.addrWidth(4), .dataWidth(2)) rom_5 (.addr(OP), .data(Acc_Src));  // open: sel
  ROM #(.addrWidth(4), .dataWidth(1)) rom_6 (.addr(OP), .data(Acc_Write));  // open: sel
  ROM #(.addrWidth(4), .dataWidth(2)) rom_7 (.addr(OP), .data(Acc_Dst));  // open: sel
  ROM #(.addrWidth(4), .dataWidth(1)) rom_8 (.addr(OP), .data(Cond_Branch));  // open: sel
  ROM #(.addrWidth(4), .dataWidth(1)) rom_9 (.addr(OP), .data(Branch));  // open: sel

  // Notes on the sheet:
  //   contents of rom_1 (hex, n*v repeats v):
  //   12*1 0 1 1 1
  //   contents of rom_2 (hex, n*v repeats v):
  //   7*0 5*1
  //   contents of rom_3 (hex, n*v repeats v):
  //   0 0 0 1 2 3 4 0 0 1 2 3
  //   contents of rom_4 (hex, n*v repeats v):
  //   15*0 1
  //   contents of rom_5 (hex, n*v repeats v):
  //   0 0 5*1 2 4*1
  //   contents of rom_6 (hex, n*v repeats v):
  //   0 11*1
  //   contents of rom_7 (hex, n*v repeats v):
  //   12*0 1 2 2 3
  //   contents of rom_8 (hex, n*v repeats v):
  //   14*0 1
  //   contents of rom_9 (hex, n*v repeats v):
  //   13*0 1
endmodule
