// Logisim project CPU2.circ as structural Verilog: 10 circuits, main circuit CPU
module CPU (
  input  [7:0] In_Port,
  input  Reset,
  input  [15:0] Pgm_Data,
  input  Pgm_Clock,
  input  Run,
  input  Ext_Clock,
  input  Clock_Select,
  output [7:0] Out_Port
);

  wire branch_1_pc_set, clock_1_execute_clock, clock_1_fetch_clock, control_1_acc, control_1_out_port,
       decoder_1_out0, decoder_1_out1, decoder_1_out2, decoder_1_out3, decoder_1_out4, decoder_1_out5,
       decoder_2_out0, decoder_2_out1, decoder_2_out2, decoder_2_out3, decoder_3_out0, decoder_3_out1,
       decoder_3_out2, decoder_3_out3, not_1_out, not_2_out, or_1_out;
  wire [0:0] control_1_sp;
  wire [1:0] control_1_addr_bus, control_1_branch, control_1_ram, control_1_sp_2;
  wire [2:0] control_1_data_bus;
  wire [3:0] control_1_alu;
  wire [4:4] control_1_alu_2;
  wire [7:0] Acc_q, controlled_buffer_1_out, controlled_buffer_2_out, controlled_buffer_3_out, pc_1_out,
       pgm_mem_1_operand_out, ram_1_data, sp_1_out;
  wire [15:0] pgm_mem_1_word_out;

  Decoder #(.select(3), .enable("false")) decoder_1 (
    .out0(decoder_1_out0), .out1(decoder_1_out1), .out2(decoder_1_out2), .out3(decoder_1_out3),
    .out4(decoder_1_out4), .out5(decoder_1_out5), .sel(control_1_data_bus));  // open: out6, out7
  // Probe on control_1_data_bus
  Decoder #(.select(2), .enable("false")) decoder_2 (
    .out0(decoder_2_out0), .out1(decoder_2_out1), .out2(decoder_2_out2), .out3(decoder_2_out3),
    .sel(control_1_addr_bus));
  Decoder #(.select(2)) decoder_3 (
    .out0(decoder_3_out0), .out1(decoder_3_out1), .out2(decoder_3_out2), .out3(decoder_3_out3),
    .sel(control_1_sp_2), .en(control_1_sp[0]));
  // Probe on control_1_addr_bus
  assign controlled_buffer_1_out = decoder_1_out0 ? In_Port : 8'bz;  // Controlled_Buffer controlled_buffer_1
  SP sp_1 (
    .Load(decoder_3_out0), .Dec(decoder_3_out1), .Inc(decoder_3_out2), .Reset(decoder_3_out3),
    .In(controlled_buffer_1_out), .Clock(clock_1_execute_clock), .Out(sp_1_out));
  assign controlled_buffer_2_out = decoder_2_out1 ? sp_1_out : 8'bz;  // Controlled_Buffer controlled_buffer_2
  Clock clock_1 (
    .Run(Run), .Ext_Clock(Ext_Clock), .Clock_Select(Clock_Select), .Reset(Reset),
    .Fetch_Clock(clock_1_fetch_clock), .Execute_Clock(clock_1_execute_clock));
  assign controlled_buffer_3_out = not_1_out ? controlled_buffer_1_out : 8'bz;  // Controlled_Buffer controlled_buffer_3
  Register Acc (.D(controlled_buffer_3_out), .en(control_1_acc), .Q(Acc_q), .clk(clock_1_execute_clock), .clr(Reset));
  assign controlled_buffer_2_out = decoder_2_out0 ? In_Port : 8'bz;  // Controlled_Buffer controlled_buffer_4
  assign controlled_buffer_1_out = decoder_1_out2 ? Acc_q : 8'bz;  // Controlled_Buffer controlled_buffer_5
  not not_1 (not_1_out, control_1_alu_2[4]);
  assign controlled_buffer_2_out = decoder_2_out2 ? Acc_q : 8'bz;  // Controlled_Buffer controlled_buffer_6
  ALU alu_1 (
    .In_B(controlled_buffer_1_out), .In_A(Acc_q), .Operation(control_1_alu), .Enable(control_1_alu_2[4]),
    .Out(controlled_buffer_3_out));
  Control control_1 (
    .Instruction(pgm_mem_1_word_out), .Data_Bus(control_1_data_bus), .Addr_Bus(control_1_addr_bus),
    .SP({control_1_sp_2, control_1_sp[0]}), .Acc(control_1_acc), .ALU({control_1_alu_2[4], control_1_alu}),
    .RAM(control_1_ram), .Branch(control_1_branch), .Out_Port(control_1_out_port));
  RAM ram_1 (
    .addr(controlled_buffer_2_out), .data(ram_1_data), .sel(control_1_ram[1]), .clk(clock_1_execute_clock),
    .ld(control_1_ram[0]), .clr(Reset));
  assign controlled_buffer_1_out = decoder_1_out3 ? ram_1_data : 8'bz;  // Controlled_Buffer controlled_buffer_7
  assign ram_1_data = not_2_out ? controlled_buffer_1_out : 8'bz;  // Controlled_Buffer controlled_buffer_8
  not not_2 (not_2_out, control_1_ram[0]);
  PC pc_1 (.In(controlled_buffer_1_out), .Set(branch_1_pc_set), .Inc(or_1_out), .Reset(Reset), .Out(pc_1_out));
  or or_1 (or_1_out, clock_1_fetch_clock, Pgm_Clock);
  Branch branch_1 (
    .Acc(Acc_q), .Branch(control_1_branch[0]), .Cond(control_1_branch[1]), .Clock(clock_1_execute_clock),
    .PC_Set(branch_1_pc_set));
  assign controlled_buffer_1_out = decoder_1_out4 ? pc_1_out : 8'bz;  // Controlled_Buffer controlled_buffer_9
  Pgm_Mem pgm_mem_1 (
    .Addr(pc_1_out), .Word_In(Pgm_Data), .Write(Pgm_Clock), .Fetch(clock_1_fetch_clock),
    .Operand_Out(pgm_mem_1_operand_out), .Word_Out(pgm_mem_1_word_out));
  assign controlled_buffer_1_out = decoder_1_out5 ? pgm_mem_1_operand_out : 8'bz;  // Controlled_Buffer controlled_buffer_10
  assign controlled_buffer_2_out = decoder_2_out3 ? pgm_mem_1_operand_out : 8'bz;  // Controlled_Buffer controlled_buffer_11
  // Probe on controlled_buffer_1_out
  // Probe on controlled_buffer_1_out
  assign controlled_buffer_1_out = decoder_1_out1 ? Out_Port : 8'bz;  // Controlled_Buffer controlled_buffer_12
  // Probe on Out_Port
  Register register_1 (
    .D(controlled_buffer_1_out), .en(control_1_out_port), .Q(Out_Port), .clk(clock_1_execute_clock),
    .clr(Reset));
  // Probe on pgm_mem_1_operand_out
  // Probe on pgm_mem_1_operand_out
  // Probe on pgm_mem_1_word_out
  // Probe on pgm_mem_1_word_out
  // Probe on controlled_buffer_2_out
  // Probe on controlled_buffer_2_out
  // Probe on clock_1_fetch_clock
  // Probe on clock_1_execute_clock

  // Notes on the sheet:
  //   Pgm_Clock: pull=down
endmodule

module PC (
  input  [7:0] In,
  input  Set,
  input  Inc,
  input  Reset,
  output [7:0] Out
);

  wire and_1_out, buffer_1_out, d_ff_1_q, or_1_out, or_2_out;

  buf buffer_1 (buffer_1_out, Inc);
  D_Flip_Flop #(.trigger("falling")) d_ff_1 (
    .clk(Inc), .D(buffer_1_out), .Q(d_ff_1_q), .reset(or_1_out));  // open: Qn, preset, en
  or or_1 (or_1_out, Set, Reset);
  and and_1 (and_1_out, Inc, d_ff_1_q);
  Counter counter_1 (.load(Set), .D(In), .count(Inc), .Q(Out), .clk(or_2_out), .clr(Reset));  // open: carry
  or or_2 (or_2_out, and_1_out, Set);

  // Notes on the sheet:
  //   In: pull=down
  //   Reset: pull=down
  //   Set: pull=down
  //   Inc: pull=down
endmodule

module ALU (
  input  [7:0] In_B,
  input  [7:0] In_A,
  input  [3:0] Operation,
  input  Enable,
  output [7:0] Out
);

  wire [2:0] bitselector_1_out, bitselector_2_out, bitselector_3_out, bitselector_4_out;
  wire [7:0] adder_1_out, and_1_out, divider_1_out, divider_1_rem, divider_2_out, divider_2_rem,
       multiplier_1_out, not_1_out, or_1_out, shifter_1_out, shifter_2_out, shifter_3_out, shifter_4_out,
       subtractor_1_out, subtractor_2_out, xor_1_out;

  BitSelector #(.group(3)) bitselector_1 (.in(In_B), .out(bitselector_1_out), .sel(2'b00));
  BitSelector #(.group(3)) bitselector_2 (.in(In_B), .out(bitselector_2_out), .sel(2'b00));
  BitSelector #(.group(3)) bitselector_3 (.in(In_B), .out(bitselector_3_out), .sel(2'b00));
  BitSelector #(.group(3)) bitselector_4 (.in(In_B), .out(bitselector_4_out), .sel(2'b00));
  Adder adder_1 (.a(In_A), .b(In_B), .out(adder_1_out));  // open: cin, cout
  Subtractor subtractor_1 (.a(In_A), .b(In_B), .out(subtractor_1_out));  // open: bin, bout
  Subtractor subtractor_2 (.a(In_B), .b(In_A), .out(subtractor_2_out));  // open: bin, bout
  Multiplier multiplier_1 (.a(In_A), .b(In_B), .out(multiplier_1_out));  // open: cin, cout
  Divider divider_1 (.a(In_A), .b(In_B), .out(divider_1_out), .rem(divider_1_rem));  // open: upper
  Divider divider_2 (.a(In_B), .b(In_A), .out(divider_2_out), .rem(divider_2_rem));  // open: upper
  Shifter shifter_1 (.in(In_A), .\dist (bitselector_1_out), .out(shifter_1_out));
  Shifter #(.shift("lr")) shifter_2 (.in(In_A), .\dist (bitselector_2_out), .out(shifter_2_out));
  Shifter #(.shift("rl")) shifter_3 (.in(In_A), .\dist (bitselector_3_out), .out(shifter_3_out));
  Shifter #(.shift("rr")) shifter_4 (.in(In_A), .\dist (bitselector_4_out), .out(shifter_4_out));
  assign and_1_out = In_A & In_B;  // AND_Gate and_1, 8 bits wide
  assign or_1_out = In_A | In_B;  // OR_Gate or_1, 8 bits wide
  assign not_1_out = ~In_A;  // NOT_Gate not_1, 8 bits wide
  assign xor_1_out = In_A ^ In_B;  // XOR_Gate xor_1, 8 bits wide
  Multiplexer #(.select(4), .width(8)) multiplexer_1 (
    .in0(adder_1_out), .in1(subtractor_1_out), .in2(subtractor_2_out), .in3(multiplier_1_out),
    .in4(divider_1_out), .in5(divider_1_rem), .in6(divider_2_out), .in7(divider_2_rem), .in8(shifter_1_out),
    .in9(shifter_2_out), .in10(shifter_3_out), .in11(shifter_4_out), .in12(and_1_out), .in13(or_1_out),
    .in14(xor_1_out), .in15(not_1_out), .out(Out), .sel(Operation), .en(Enable));

  // Notes on the sheet:
  //   Enable: pull=down
endmodule

// Pgm
module Pgm_Mem (
  input  Write,
  input  [15:0] Word_In,
  input  [7:0] Addr,
  input  Fetch,
  output [7:0] Operand_Out,
  output [15:0] Word_Out
);

  wire pull_resistor_1_node;
  wire [15:0] ram_1_data;

  RAM #(.dataWidth(16), .bus("separate")) ram_1 (
    .addr(Addr), .din(Word_In), .data(ram_1_data), .str(Write), .clk(Write), .ld(Fetch));  // open: sel, clr
  Register #(.width(16), .trigger("low")) register_1 (
    .D(ram_1_data), .Q({Word_Out[15:8], Operand_Out}), .clk(pull_resistor_1_node));  // open: en, clr
  Pull_Resistor pull_resistor_1 (.node(pull_resistor_1_node));

  assign Word_Out[7:0] = Operand_Out;

  // Notes on the sheet:
  //   Fetch: pull=down
  //   Write: pull=down
endmodule

module Control (
  input  [15:0] Instruction,
  output [2:0] Data_Bus,
  output [1:0] Addr_Bus,
  output [2:0] SP,
  output Acc,
  output [4:0] ALU,
  output [1:0] RAM,
  output [1:0] Branch,
  output Out_Port
);

  wire Acc_Src, and_3_out, and_5_out, and_6_out, and_7_out, and_8_out, and_9_out, and_10_out, and_12_out,
       and_13_out, and_14_out, and_15_out, and_16_out, and_17_out, and_18_out, and_19_out, and_20_out,
       and_24_out, and_25_out, and_26_out, comparator_1_eq, comparator_2_eq, comparator_3_eq,
       comparator_4_eq, comparator_5_eq, comparator_6_eq, comparator_7_eq, Dst_Dir, Dst_Ind, Lit_Dst,
       Lit_Src, Reg_Dst, Reg_Src, Src_Dir;
  wire [1:0] bitselector_4_out;
  wire [2:0] bitselector_3_out;
  wire [3:0] swapper_1_high, swapper_1_lo, Trgt_Reg;
  wire [7:0] not_1_out;

  BitSelector #(.group(4)) bitselector_1 (.in(Instruction[15:8]), .out(ALU[3:0]), .sel(1'b0));
  assign {not_1_out[7:6], Src_Dir, not_1_out[4:0]} = ~Instruction[15:8];  // NOT_Gate not_1, 8 bits wide
  and and_1 (Lit_Dst, not_1_out[0], not_1_out[1], not_1_out[6]);
  BitSelector #(.group(4)) bitselector_2 (.in(Instruction[7:0]), .out(Trgt_Reg), .sel(1'b0));
  Swapper swapper_1 (.In(Instruction[7:0]), .Swap(Instruction[13]), .High(swapper_1_high), .Lo(swapper_1_lo));
  and and_2 (Dst_Ind, Instruction[12], not_1_out[6]);
  and and_3 (and_3_out, not_1_out[2], not_1_out[3], not_1_out[6]);
  or or_1 (Lit_Src, and_3_out, and_5_out);
  BitSelector #(.width(4), .group(3)) bitselector_3 (.in(swapper_1_high), .out(bitselector_3_out), .sel(1'b0));
  BitSelector #(.width(4), .group(2)) bitselector_4 (.in(swapper_1_lo), .out(bitselector_4_out), .sel(1'b0));
  and and_4 (Reg_Dst, Instruction[9], not_1_out[6]);
  and and_5 (and_5_out, not_1_out[4], Instruction[14]);
  and and_6 (and_6_out, Reg_Src, Src_Dir);
  and and_7 (and_7_out, Instruction[13], Reg_Src);
  and and_8 (and_8_out, Reg_Dst, Dst_Ind);
  or or_2 (Reg_Src, and_10_out, and_9_out);
  and and_9 (and_9_out, Instruction[11], not_1_out[6]);
  and and_10 (and_10_out, Instruction[14], Instruction[12]);
  or or_3 (Dst_Dir, Instruction[14], not_1_out[4]);
  assign Data_Bus = and_6_out ? bitselector_3_out : 3'bz;  // Controlled_Buffer controlled_buffer_1
  assign Addr_Bus = and_7_out ? bitselector_4_out : 2'bz;  // Controlled_Buffer controlled_buffer_2
  assign Addr_Bus = and_8_out ? bitselector_4_out : 2'bz;  // Controlled_Buffer controlled_buffer_3
  and and_11 (Acc_Src, Instruction[10], not_1_out[6]);
  assign Data_Bus = and_12_out ? 3'b101 : 3'bz;  // Controlled_Buffer controlled_buffer_4
  and and_12 (and_12_out, Lit_Src, Src_Dir);
  and and_13 (and_13_out, Instruction[13], Lit_Src);
  assign Addr_Bus = and_13_out ? 2'b11 : 2'bz;  // Controlled_Buffer controlled_buffer_5
  assign Addr_Bus = and_14_out ? 2'b11 : 2'bz;  // Controlled_Buffer controlled_buffer_6
  and and_14 (and_14_out, Lit_Dst, Dst_Ind);
  assign Data_Bus = and_15_out ? 3'b010 : 3'bz;  // Controlled_Buffer controlled_buffer_7
  and and_15 (and_15_out, Acc_Src, Src_Dir);
  and and_16 (and_16_out, Instruction[13], Acc_Src);
  assign Addr_Bus = and_16_out ? 2'b10 : 2'bz;  // Controlled_Buffer controlled_buffer_8
  assign Addr_Bus = and_17_out ? 2'b10 : 2'bz;  // Controlled_Buffer controlled_buffer_9
  and and_17 (and_17_out, Instruction[8], Dst_Ind);
  Comparator #(.width(4)) comparator_1 (.a(Trgt_Reg), .b(4'b0001), .eq(comparator_1_eq));  // open: gt, lt
  or or_4 (RAM[1], Instruction[13], Dst_Ind);
  assign Data_Bus = Instruction[13] ? 3'b011 : 3'bz;  // Controlled_Buffer controlled_buffer_10
  and and_18 (and_18_out, Dst_Dir, Instruction[8]);
  and and_19 (and_19_out, Dst_Dir, Reg_Dst, comparator_1_eq);
  or or_5 (Acc, Instruction[14], and_18_out, and_19_out);
  and and_20 (and_20_out, Reg_Dst, Dst_Dir);
  Comparator #(.width(4)) comparator_2 (.a(Trgt_Reg), .b(4'b0010), .eq(comparator_2_eq));  // open: gt, lt
  Comparator #(.width(4)) comparator_3 (.a(Trgt_Reg), .b(4'b1001), .eq(comparator_3_eq));  // open: gt, lt
  Comparator #(.width(4)) comparator_4 (.a(Trgt_Reg), .b(4'b0011), .eq(comparator_4_eq));  // open: gt, lt
  Comparator #(.width(4)) comparator_5 (.a(Trgt_Reg), .b(4'b0100), .eq(comparator_5_eq));  // open: gt, lt
  Comparator #(.width(4)) comparator_6 (.a(Trgt_Reg), .b(4'b1010), .eq(comparator_6_eq));  // open: gt, lt
  Comparator #(.width(3)) comparator_7 (.a(Data_Bus), .b(3'b100), .eq(comparator_7_eq));  // open: gt, lt
  and and_21 (Branch[0], and_20_out, comparator_2_eq);
  and and_22 (Branch[1], and_20_out, comparator_3_eq);
  and and_23 (Out_Port, and_20_out, comparator_4_eq);
  and and_24 (and_24_out, and_20_out, comparator_5_eq);
  assign SP[2:1] = and_24_out ? 2'b00 : 2'bz;  // Controlled_Buffer controlled_buffer_11
  and and_25 (and_25_out, and_20_out, comparator_6_eq);
  assign SP[2:1] = and_25_out ? 2'b10 : 2'bz;  // Controlled_Buffer controlled_buffer_12
  and and_26 (and_26_out, Src_Dir, Reg_Src, comparator_7_eq);
  assign SP[2:1] = and_26_out ? 2'b01 : 2'bz;  // Controlled_Buffer controlled_buffer_13
  or or_6 (SP[0], and_24_out, and_25_out, and_26_out);

  assign ALU[4] = Instruction[14];
  assign RAM[0] = Instruction[13];

  // Other names for the same wires on the sheet: Addr[1:0] = Addr_Bus; Data[2:0] = Data_Bus; Acc_Dst = Instruction[8];
  //   Out = Out_Port; Src_Ind = Instruction[13]
endmodule

module Branch (
  input  [7:0] Acc,
  input  Branch,
  input  Cond,
  input  Clock,
  output PC_Set
);

  wire and_1_out, comparator_1_eq, or_1_out;

  Comparator comparator_1 (.a(Acc), .b({8{1'b0}}), .eq(comparator_1_eq));  // open: gt, lt
  and and_1 (and_1_out, Cond, comparator_1_eq);
  or or_1 (or_1_out, Branch, and_1_out);
  and and_2 (PC_Set, or_1_out, Clock);
endmodule

module SP (
  input  [7:0] In,
  input  Load,
  input  Dec,
  input  Inc,
  input  Reset,
  input  Clock,
  output [7:0] Out
);

  wire and_1_out, buffer_1_out, or_1_out, or_2_out, or_3_out, or_4_out;

  or or_1 (or_1_out, Load, Inc);
  or or_2 (or_2_out, Load, Dec);
  or or_3 (or_3_out, Dec, Inc);
  buf buffer_1 (buffer_1_out, Dec);
  Counter counter_1 (.load(or_2_out), .D(In), .count(or_3_out), .Q(Out), .clk(or_4_out), .clr(Reset));  // open: carry
  or or_4 (or_4_out, buffer_1_out, and_1_out);
  and and_1 (and_1_out, or_1_out, Clock);
endmodule

// Clk
module Clock (
  input  Run,
  input  Ext_Clock,
  input  Clock_Select,
  input  Reset,
  output Fetch_Clock,
  output Execute_Clock
);

  wire clock_1_out, multiplexer_1_out;

  Clock_part clock_1 (.out(clock_1_out));
  Multiplexer multiplexer_1 (.in0(clock_1_out), .in1(Ext_Clock), .out(multiplexer_1_out), .sel(Clock_Select), .en(Run));
  T_Flip_Flop t_ff_1 (
    .clk(multiplexer_1_out), .T(1'b1), .Q(Fetch_Clock), .Qn(Execute_Clock), .reset(Reset));  // open: preset, en

  // Notes on the sheet:
  //   Clock_Select: pull=down
endmodule

// Swp
module Swapper (
  input  [7:0] In,
  input  Swap,
  output [3:0] High,
  output [3:0] Lo
);

  Multiplexer #(.width(4), .enable("false")) multiplexer_1 (.in0(In[7:4]), .in1(In[3:0]), .out(High), .sel(Swap));
  Multiplexer #(.width(4), .enable("false")) multiplexer_2 (.in0(In[3:0]), .in1(In[7:4]), .out(Lo), .sel(Swap));

  // Notes on the sheet:
  //   Swap: pull=down
endmodule

module Board (
  input  [15:0] in_1,
  input  in_2,
  input  in_3
);

  wire button_1_out, button_2_out, button_3_out;
  wire [7:0] cpu_1_out_port;

  Button button_1 (.out(button_1_out));
  Button button_2 (.out(button_2_out));
  Button button_3 (.out(button_3_out));
  CPU cpu_1 (
    .Reset(button_1_out), .Pgm_Data(in_1), .Pgm_Clock(button_3_out), .Run(in_2), .Ext_Clock(button_2_out),
    .Clock_Select(in_3), .Out_Port(cpu_1_out_port));  // open: In_Port
  // Probe on cpu_1_out_port
  // Probe on cpu_1_out_port
  // Probe on cpu_1_out_port
endmodule
