// Logisim project CPU3.circ as structural Verilog: 13 circuits, main circuit CPU
module CPU (
  input  [7:0] In_Port,
  input  In_Port_Trigger,
  input  Reset,
  input  Run,
  input  Ext_Clock,
  input  Clock_Select,
  output In_Port_Read,
  output [7:0] Out_Port,
  output Out_Trigger
);

  wire buffer_1_out, buffer_2_out, buffer_3_out, buffer_4_out, buffer_5_out, buffer_6_out,
       clock_1_execute_clock, clock_1_fetch_clock, control_1_acc, control_1_bcc, control_1_execute,
       control_1_out_port, decoder_1_out0, decoder_1_out1, decoder_1_out2, decoder_1_out3, decoder_1_out4,
       decoder_1_out5, decoder_1_out6, decoder_2_out0, decoder_2_out1, decoder_2_out2, decoder_2_out3,
       decoder_2_out4, decoder_2_out5, decoder_3_out0, decoder_3_out1, decoder_3_out2, decoder_3_out3,
       falling_edge_1_trigger, falling_edge_2_trigger, falling_edge_3_trigger, not_1_out, not_2_out,
       or_1_out, pull_resistor_1_node, s_r_ff_1_q, s_r_ff_1_qn;
  wire [0:0] control_1_sp;
  wire [1:0] control_1_ram, control_1_sp_2, instruction_buffer_1_word_count_out;
  wire [2:0] control_1_addr_bus, control_1_data_bus;
  wire [3:0] control_1_alu;
  wire [4:4] control_1_alu_2;
  wire [5:0] control_1_branch;
  wire [6:0] bit_extender_1_out;
  wire [7:0] Acc_q, controlled_buffer_1_out, controlled_buffer_2_out, controlled_buffer_3_out,
       controlled_buffer_9_out, GP_q, instruction_buffer_1_operand_out, pc_2_out, register_1_q, register_2_q,
       sp_1_out;
  wire [15:0] instruction_buffer_1_instruction_out;

  Decoder #(.select(3), .enable("false")) decoder_1 (
    .out0(decoder_1_out0), .out1(decoder_1_out1), .out2(decoder_1_out2), .out3(decoder_1_out3),
    .out4(decoder_1_out4), .out5(decoder_1_out5), .out6(decoder_1_out6), .sel(control_1_data_bus));  // open: out7
  // Probe on control_1_data_bus
  Decoder #(.select(3), .enable("false")) decoder_2 (
    .out0(decoder_2_out0), .out1(decoder_2_out1), .out2(decoder_2_out2), .out3(decoder_2_out3),
    .out4(decoder_2_out4), .out5(decoder_2_out5), .sel(control_1_addr_bus));  // open: out6, out7
  Decoder #(.select(2)) decoder_3 (
    .out0(decoder_3_out0), .out1(decoder_3_out1), .out2(decoder_3_out2), .out3(decoder_3_out3),
    .sel(control_1_sp_2), .en(control_1_sp[0]));
  // Probe on control_1_addr_bus
  Register register_1 (.D(In_Port), .Q(register_1_q), .clk(In_Port_Trigger), .clr(In_Port_Read));  // open: en
  assign controlled_buffer_1_out = decoder_1_out0 ? register_1_q : 8'bz;  // Controlled_Buffer controlled_buffer_1
  SP sp_1 (
    .Set(decoder_3_out0), .Dec(decoder_3_out1), .Inc(decoder_3_out2), .Reset(decoder_3_out3),
    .In(controlled_buffer_1_out), .Clock(clock_1_execute_clock), .Out(sp_1_out));
  // Probe on sp_1_out
  assign controlled_buffer_2_out = decoder_2_out1 ? sp_1_out : 8'bz;  // Controlled_Buffer controlled_buffer_2
  Clock clock_1 (
    .Run(Run), .Ext_Clock(Ext_Clock), .Clock_Select(Clock_Select), .Reset(Reset),
    .Execute(control_1_execute), .Fetch_Clock(clock_1_fetch_clock), .Execute_Clock(clock_1_execute_clock));
  Pull_Resistor pull_resistor_1 (.node(pull_resistor_1_node));
  assign controlled_buffer_3_out = not_1_out ? controlled_buffer_1_out : 8'bz;  // Controlled_Buffer controlled_buffer_3
  assign controlled_buffer_2_out = decoder_2_out0 ? register_1_q : 8'bz;  // Controlled_Buffer controlled_buffer_4
  S_R_Flip_Flop #(.trigger("falling")) s_r_ff_1 (
    .S(pull_resistor_1_node), .clk(clock_1_execute_clock), .R(decoder_1_out0), .Q(s_r_ff_1_q),
    .Qn(s_r_ff_1_qn), .preset(In_Port_Trigger));  // open: reset, en
  assign controlled_buffer_1_out = decoder_1_out2 ? Acc_q : 8'bz;  // Controlled_Buffer controlled_buffer_5
  Register #(.trigger("falling")) Acc (
    .D(controlled_buffer_3_out), .en(control_1_acc), .Q(Acc_q), .clk(clock_1_execute_clock), .clr(Reset));
  assign controlled_buffer_2_out = decoder_2_out2 ? Acc_q : 8'bz;  // Controlled_Buffer controlled_buffer_6
  Rising_Edge rising_edge_1 (.Clock(s_r_ff_1_qn), .Trigger(In_Port_Read));
  not not_1 (not_1_out, control_1_alu_2[4]);
  ALU alu_1 (
    .In_B(controlled_buffer_1_out), .In_A(Acc_q), .Operation(control_1_alu), .Enable(control_1_alu_2[4]),
    .Out(controlled_buffer_3_out));
  assign controlled_buffer_1_out = decoder_1_out3 ? GP_q : 8'bz;  // Controlled_Buffer controlled_buffer_7
  Register #(.trigger("falling")) GP (
    .D(controlled_buffer_1_out), .en(control_1_bcc), .Q(GP_q), .clk(clock_1_execute_clock), .clr(Reset));
  assign controlled_buffer_2_out = decoder_2_out3 ? GP_q : 8'bz;  // Controlled_Buffer controlled_buffer_8
  Falling_Edge falling_edge_1 (.Clock(clock_1_execute_clock), .Trigger(falling_edge_1_trigger));
  Control control_1 (
    .Execute(control_1_execute), .Fetch_Clock(clock_1_fetch_clock),
    .Instruction_In(instruction_buffer_1_instruction_out),
    .Word_Count_In(instruction_buffer_1_word_count_out), .Data_Bus(control_1_data_bus),
    .Addr_Bus(control_1_addr_bus), .SP({control_1_sp_2, control_1_sp[0]}), .Acc(control_1_acc),
    .ALU({control_1_alu_2[4], control_1_alu}), .Bcc(control_1_bcc), .RAM(control_1_ram),
    .Branch(control_1_branch), .Out_Port(control_1_out_port));
  assign controlled_buffer_9_out = not_2_out ? controlled_buffer_1_out : 8'bz;  // Controlled_Buffer controlled_buffer_9
  RAM ram_1 (
    .addr(controlled_buffer_2_out), .data(controlled_buffer_9_out), .sel(control_1_ram[1]),
    .clk(falling_edge_1_trigger), .ld(control_1_ram[0]));  // open: clr
  not not_2 (not_2_out, control_1_ram[0]);
  assign controlled_buffer_1_out = decoder_1_out4 ? register_2_q : 8'bz;  // Controlled_Buffer controlled_buffer_10
  Register #(.trigger("high")) register_2 (
    .D(controlled_buffer_9_out), .Q(register_2_q), .clk(control_1_ram[0]));  // open: en, clr
  Falling_Edge falling_edge_2 (.Clock(clock_1_execute_clock), .Trigger(falling_edge_2_trigger));
  // Probe on instruction_buffer_1_word_count_out
  Instruction_Buffer instruction_buffer_1 (
    .Word_In(controlled_buffer_1_out), .Operand_Out(instruction_buffer_1_operand_out),
    .Clock(clock_1_fetch_clock), .Reset_Count(or_1_out),
    .Instruction_Out(instruction_buffer_1_instruction_out),
    .Word_Count_Out(instruction_buffer_1_word_count_out));  // open: Reset_Data
  // Probe on instruction_buffer_1_instruction_out
  assign controlled_buffer_1_out = decoder_1_out5 ? pc_2_out : 8'bz;  // Controlled_Buffer controlled_buffer_11
  // Probe on pc_2_out
  PC pc_2 (
    .In(controlled_buffer_1_out), .Acc_In(Acc_q), .GP_In(GP_q), .In_Port_Changed(s_r_ff_1_q),
    .Branch(control_1_branch[5]), .Cond(control_1_branch[4]), .Add_3(control_1_branch[3]),
    .Cond_Op(control_1_branch[2:0]), .Execute_Clock(clock_1_execute_clock),
    .Fetch_Clock(clock_1_fetch_clock), .Reset(Reset), .Out(pc_2_out));
  assign controlled_buffer_2_out = decoder_2_out4 ? pc_2_out : 8'bz;  // Controlled_Buffer controlled_buffer_12
  or or_1 (or_1_out, falling_edge_2_trigger, Reset);
  assign controlled_buffer_1_out = decoder_1_out6 ? instruction_buffer_1_operand_out : 8'bz;  // Controlled_Buffer controlled_buffer_13
  assign controlled_buffer_2_out = decoder_2_out5 ? instruction_buffer_1_operand_out : 8'bz;  // Controlled_Buffer controlled_buffer_14
  Register #(.trigger("falling")) register_3 (
    .D(controlled_buffer_1_out), .en(control_1_out_port), .Q(Out_Port), .clk(clock_1_execute_clock),
    .clr(Reset));
  // Probe on controlled_buffer_1_out
  // Probe on controlled_buffer_1_out
  assign controlled_buffer_1_out = decoder_1_out1 ? Out_Port : 8'bz;  // Controlled_Buffer controlled_buffer_15
  // Probe on Out_Port
  buf buffer_1 (buffer_1_out, buffer_2_out);
  buf buffer_2 (buffer_2_out, buffer_3_out);
  Falling_Edge falling_edge_3 (.Clock(clock_1_execute_clock), .Trigger(falling_edge_3_trigger));
  buf buffer_3 (buffer_3_out, buffer_5_out);
  buf buffer_4 (buffer_4_out, falling_edge_3_trigger);
  buf buffer_5 (buffer_5_out, buffer_6_out);
  buf buffer_6 (buffer_6_out, buffer_4_out);
  // Probe on controlled_buffer_2_out
  // Probe on controlled_buffer_2_out
  // Probe on clock_1_execute_clock
  // Probe on clock_1_fetch_clock
  // Probe on instruction_buffer_1_operand_out
  // Probe on instruction_buffer_1_operand_out
  Bit_Extender #(.out_width(7)) bit_extender_1 (.in(Out_Port), .out(bit_extender_1_out));
  and and_1 (Out_Trigger, control_1_out_port, buffer_1_out);
  TTY tty_1 (.data(bit_extender_1_out), .clk(Out_Trigger), .clr(Reset));  // open: we
endmodule

// CTRL
module Control (
  input  [1:0] Word_Count_In,
  input  Fetch_Clock,
  input  [15:0] Instruction_In,
  output Execute,
  output [2:0] Data_Bus,
  output [2:0] Addr_Bus,
  output [2:0] SP,
  output Acc,
  output [4:0] ALU,
  output Bcc,
  output [1:0] RAM,
  output [5:0] Branch,
  output Out_Port
);

  wire and_5_out, and_8_out, and_9_out, and_10_out, comparator_1_eq, comparator_2_eq, comparator_3_eq,
       comparator_4_eq, comparator_5_eq, Cond, Dst_Dir, No_Operand, pull_resistor_1_node, s_r_ff_1_q, SP_Dec,
       SP_Inc, Src_Dir;
  wire [1:1] or_1_out;
  wire [2:0] multiplexer_2_out, swapper_1_high, swapper_1_lo, Trgt_Reg;
  wire [5:0] bitselector_3_out, not_2_out;
  wire [6:0] not_1_out;

  BitSelector #(.group(4)) bitselector_1 (.in(Instruction_In[15:8]), .out(ALU[3:0]), .sel(1'b0));
  assign {No_Operand, not_1_out} = ~Instruction_In[15:8];  // NOT_Gate not_1, 8 bits wide
  assign {Src_Dir, Dst_Dir, not_2_out} = ~Instruction_In[7:0];  // NOT_Gate not_2, 8 bits wide
  BitSelector #(.group(3)) bitselector_2 (.in(Instruction_In[7:0]), .out(Trgt_Reg), .sel(2'b00));
  BitSelector #(.group(6)) bitselector_3 (.in(Instruction_In[7:0]), .out(bitselector_3_out), .sel(1'b0));
  Pull_Resistor pull_resistor_1 (.node(pull_resistor_1_node));
  and and_1 (SP_Inc, Instruction_In[13], not_1_out[4]);
  and and_2 (SP_Dec, Instruction_In[13], Instruction_In[12]);
  Swapper swapper_1 (.In(bitselector_3_out), .Swap(Instruction_In[7]), .High(swapper_1_high), .Lo(swapper_1_lo));
  S_R_Flip_Flop #(.trigger("low")) s_r_ff_1 (
    .S(Execute), .clk(pull_resistor_1_node), .R(Fetch_Clock), .Q(s_r_ff_1_q));  // open: Qn, preset, reset, en
  Multiplexer #(.width(3), .enable("false")) multiplexer_1 (
    .in0(3'b100), .in1(swapper_1_lo), .out(Addr_Bus), .sel(s_r_ff_1_q));
  and and_3 (Cond, not_1_out[5], Instruction_In[12]);
  or or_1 (or_1_out[1], Instruction_In[7], Instruction_In[6]);
  Multiplexer #(.width(3), .enable("false")) multiplexer_2 (
    .in0(swapper_1_high), .in1(3'b100), .out(multiplexer_2_out), .sel(Instruction_In[7]));
  Multiplexer #(.width(3), .enable("false")) multiplexer_3 (
    .in0(3'b100), .in1(multiplexer_2_out), .out(Data_Bus), .sel(s_r_ff_1_q));
  Multiplexer #(.width(2), .enable("false")) multiplexer_4 (
    .in0(2'b11), .in1({or_1_out[1], Instruction_In[7]}), .out(RAM), .sel(s_r_ff_1_q));
  Comparator #(.width(3)) comparator_1 (.a(Trgt_Reg), .b(3'b100), .eq(comparator_1_eq));  // open: gt, lt
  Comparator #(.width(3)) comparator_2 (.a(Trgt_Reg), .b(3'b011), .eq(comparator_2_eq));  // open: gt, lt
  Comparator #(.width(3)) comparator_3 (.a(Trgt_Reg), .b(3'b010), .eq(comparator_3_eq));  // open: gt, lt
  Comparator #(.width(3)) comparator_4 (.a(Trgt_Reg), .b(3'b001), .eq(comparator_4_eq));  // open: gt, lt
  Comparator #(.width(3)) comparator_5 (.a(Trgt_Reg), .b(3'b000), .eq(comparator_5_eq));  // open: gt, lt
  and and_4 (Out_Port, Dst_Dir, comparator_1_eq);
  Decoder #(.disabled(0)) decoder_1 (.out0(Branch[5]), .out1(Branch[4]), .sel(Cond), .en(and_5_out));
  and and_5 (and_5_out, Dst_Dir, comparator_2_eq);
  and and_6 (Bcc, Dst_Dir, comparator_3_eq);
  and and_7 (Acc, Dst_Dir, comparator_4_eq);
  and and_8 (and_8_out, Dst_Dir, comparator_5_eq);
  assign SP[2:1] = and_8_out ? 2'b00 : 2'bz;  // Controlled_Buffer controlled_buffer_1
  assign SP[2:1] = SP_Inc ? 2'b10 : 2'bz;  // Controlled_Buffer controlled_buffer_2
  assign SP[2:1] = SP_Dec ? 2'b01 : 2'bz;  // Controlled_Buffer controlled_buffer_3
  and and_9 (and_9_out, Word_Count_In[0], Word_Count_In[1], Instruction_In[15]);
  and and_10 (and_10_out, Word_Count_In[1], No_Operand);
  or or_2 (SP[0], and_8_out, SP_Inc, SP_Dec);
  or or_3 (Execute, and_9_out, and_10_out);

  assign ALU[4] = Instruction_In[14];
  assign Branch[3:0] = Instruction_In[11:8];

  // Other names for the same wires on the sheet: Src_Ind = Instruction_In[7]; Addr[2:0] = Addr_Bus;
  //   Cond_Op[2:0] = Instruction_In[10:8]; Add_3 = Instruction_In[11]; Data[2:0] = Data_Bus;
  //   Dst_Ind = Instruction_In[6]; Operand = Instruction_In[15]; Out = Out_Port; Word_Count[1:0] = Word_Count_In
endmodule

module PC (
  input  [7:0] In,
  input  [7:0] Acc_In,
  input  [7:0] GP_In,
  input  In_Port_Changed,
  input  Branch,
  input  Cond,
  input  Add_3,
  input  [2:0] Cond_Op,
  input  Execute_Clock,
  input  Fetch_Clock,
  input  Reset,
  output [7:0] Out
);

  wire and_1_out, and_2_out, buffer_1_out, buffer_2_out, buffer_3_out, buffer_4_out, buffer_5_out,
       buffer_6_out, buffer_7_out, buffer_8_out, comparator_1_eq, comparator_1_gt, comparator_1_lt,
       falling_edge_1_trigger, multiplexer_3_out, multiplexer_4_out, or_1_out, or_2_out, or_3_out, or_4_out,
       trigger_delay_1_trigger_out;
  wire [7:0] adder_1_out, multiplexer_1_out, multiplexer_2_out;

  Adder adder_1 (.a(In), .b(8'h3), .out(adder_1_out));  // open: cin, cout
  Multiplexer #(.width(8), .enable("false")) multiplexer_1 (
    .in0(In), .in1(adder_1_out), .out(multiplexer_1_out), .sel(Add_3));
  Multiplexer #(.width(8), .enable("false")) multiplexer_2 (
    .in0({8{1'b0}}), .in1(GP_In), .out(multiplexer_2_out), .sel(Cond_Op[2]));
  Comparator comparator_1 (
    .a(Acc_In), .b(multiplexer_2_out), .gt(comparator_1_gt), .eq(comparator_1_eq), .lt(comparator_1_lt));
  and and_1 (and_1_out, multiplexer_4_out, Cond);
  Multiplexer #(.enable("false")) multiplexer_3 (
    .in0(comparator_1_eq), .in1(or_1_out), .out(multiplexer_3_out), .sel(Cond_Op[1]));
  or or_1 (or_1_out, comparator_1_gt, comparator_1_lt);
  or or_2 (or_2_out, Branch, and_1_out);
  Multiplexer #(.enable("false")) multiplexer_4 (
    .in0(multiplexer_3_out), .in1(In_Port_Changed), .out(multiplexer_4_out), .sel(Cond_Op[0]));
  and and_2 (and_2_out, or_2_out, Execute_Clock);
  buf buffer_1 (buffer_1_out, and_2_out);
  buf buffer_2 (buffer_2_out, buffer_5_out);
  buf buffer_3 (buffer_3_out, buffer_1_out);
  buf buffer_4 (buffer_4_out, buffer_2_out);
  buf buffer_5 (buffer_5_out, buffer_3_out);
  buf buffer_6 (buffer_6_out, buffer_7_out);
  buf buffer_7 (buffer_7_out, buffer_8_out);
  buf buffer_8 (buffer_8_out, buffer_4_out);
  Trigger_Delay trigger_delay_1 (.Clock(Fetch_Clock), .Reset(or_3_out), .Trigger_Out(trigger_delay_1_trigger_out));
  or or_3 (or_3_out, Execute_Clock, Reset);
  Counter counter_1 (
    .load(buffer_6_out), .D(multiplexer_1_out), .count(Fetch_Clock), .Q(Out), .clk(or_4_out), .clr(Reset));  // open: carry
  or or_4 (or_4_out, trigger_delay_1_trigger_out, falling_edge_1_trigger);
  Falling_Edge falling_edge_1 (.Clock(and_2_out), .Trigger(falling_edge_1_trigger));

  // Notes on the sheet:
  //   Reset: pull=down
  //   Fetch_Clock: pull=down
  //   In: pull=down
endmodule

module ALU (
  input  [7:0] In_B,
  input  [7:0] In_A,
  input  [3:0] Operation,
  input  Enable,
  output [7:0] Out
);

  wire [2:0] bitselector_1_out, bitselector_2_out, bitselector_3_out, bitselector_4_out;
  wire [7:0] adder_1_out, and_1_out, divider_1_out, divider_1_rem, divider_2_out, divider_2_rem,
       multiplier_1_out, not_1_out, or_1_out, shifter_1_out, shifter_2_out, shifter_3_out, shifter_4_out,
       subtractor_1_out, subtractor_2_out, xor_1_out;

  BitSelector #(.group(3)) bitselector_1 (.in(In_B), .out(bitselector_1_out), .sel(2'b00));
  BitSelector #(.group(3)) bitselector_2 (.in(In_B), .out(bitselector_2_out), .sel(2'b00));
  BitSelector #(.group(3)) bitselector_3 (.in(In_B), .out(bitselector_3_out), .sel(2'b00));
  BitSelector #(.group(3)) bitselector_4 (.in(In_B), .out(bitselector_4_out), .sel(2'b00));
  Adder adder_1 (.a(In_A), .b(In_B), .out(adder_1_out));  // open: cin, cout
  Subtractor subtractor_1 (.a(In_A), .b(In_B), .out(subtractor_1_out));  // open: bin, bout
  Subtractor subtractor_2 (.a(In_B), .b(In_A), .out(subtractor_2_out));  // open: bin, bout
  Multiplier multiplier_1 (.a(In_A), .b(In_B), .out(multiplier_1_out));  // open: cin, cout
  Divider divider_1 (.a(In_A), .b(In_B), .out(divider_1_out), .rem(divider_1_rem));  // open: upper
  Divider divider_2 (.a(In_B), .b(In_A), .out(divider_2_out), .rem(divider_2_rem));  // open: upper
  Shifter shifter_1 (.in(In_A), .\dist (bitselector_1_out), .out(shifter_1_out));
  Shifter #(.shift("lr")) shifter_2 (.in(In_A), .\dist (bitselector_2_out), .out(shifter_2_out));
  Shifter #(.shift("rl")) shifter_3 (.in(In_A), .\dist (bitselector_3_out), .out(shifter_3_out));
  Shifter #(.shift("rr")) shifter_4 (.in(In_A), .\dist (bitselector_4_out), .out(shifter_4_out));
  assign and_1_out = In_A & In_B;  // AND_Gate and_1, 8 bits wide
  assign or_1_out = In_A | In_B;  // OR_Gate or_1, 8 bits wide
  assign not_1_out = ~In_A;  // NOT_Gate not_1, 8 bits wide
  assign xor_1_out = In_A ^ In_B;  // XOR_Gate xor_1, 8 bits wide
  Multiplexer #(.select(4), .width(8)) multiplexer_1 (
    .in0(adder_1_out), .in1(subtractor_1_out), .in2(subtractor_2_out), .in3(multiplier_1_out),
    .in4(divider_1_out), .in5(divider_1_rem), .in6(divider_2_out), .in7(divider_2_rem), .in8(shifter_1_out),
    .in9(shifter_2_out), .in10(shifter_3_out), .in11(shifter_4_out), .in12(and_1_out), .in13(or_1_out),
    .in14(xor_1_out), .in15(not_1_out), .out(Out), .sel(Operation), .en(Enable));

  // Notes on the sheet:
  //   Enable: pull=down
endmodule

module Branch (
  input  [7:0] Acc,
  input  Branch,
  input  Cond,
  input  Clock,
  output PC_Set
);

  wire and_1_out, comparator_1_eq, or_1_out;

  Comparator comparator_1 (.a(Acc), .b({8{1'b0}}), .eq(comparator_1_eq));  // open: gt, lt
  and and_1 (and_1_out, Cond, comparator_1_eq);
  or or_1 (or_1_out, Branch, and_1_out);
  and and_2 (PC_Set, or_1_out, Clock);
endmodule

module SP (
  input  [7:0] In,
  input  Set,
  input  Dec,
  input  Inc,
  input  Reset,
  input  Clock,
  output [7:0] Out
);

  wire and_1_out, and_2_out, buffer_1_out, buffer_2_out, buffer_3_out, falling_edge_1_trigger, or_1_out,
       or_2_out, or_3_out, or_4_out, rising_edge_1_trigger;

  or or_1 (or_1_out, Set, Inc);
  or or_2 (or_2_out, Set, Dec);
  or or_3 (or_3_out, Dec, Inc);
  Counter #(.trigger("falling")) counter_1 (
    .load(or_2_out), .D(In), .count(or_3_out), .Q(Out), .clk(or_4_out), .clr(Reset));  // open: carry
  or or_4 (or_4_out, rising_edge_1_trigger, falling_edge_1_trigger);
  Rising_Edge rising_edge_1 (.Clock(and_1_out), .Trigger(rising_edge_1_trigger));
  Falling_Edge falling_edge_1 (.Clock(and_2_out), .Trigger(falling_edge_1_trigger));
  and and_1 (and_1_out, Dec, buffer_1_out);
  and and_2 (and_2_out, buffer_1_out, or_1_out);
  buf buffer_1 (buffer_1_out, buffer_2_out);
  buf buffer_2 (buffer_2_out, buffer_3_out);
  buf buffer_3 (buffer_3_out, Clock);
endmodule

// Clk
module Clock (
  input  Run,
  input  Ext_Clock,
  input  Clock_Select,
  input  Reset,
  input  Execute,
  output Fetch_Clock,
  output Execute_Clock
);

  wire clock_1_out, multiplexer_1_out, t_ff_1_q;

  Clock_part clock_1 (.out(clock_1_out));
  Multiplexer multiplexer_1 (.in0(clock_1_out), .in1(Ext_Clock), .out(multiplexer_1_out), .sel(Clock_Select), .en(Run));
  Demultiplexer #(.enable("false")) demultiplexer_1 (
    .out0(Fetch_Clock), .out1(Execute_Clock), .in(t_ff_1_q), .sel(Execute));
  T_Flip_Flop t_ff_1 (.clk(multiplexer_1_out), .T(1'b1), .Q(t_ff_1_q), .reset(Reset));  // open: Qn, preset, en

  // Notes on the sheet:
  //   Clock_Select: pull=down
endmodule

// Swp
module Swapper (
  input  [5:0] In,
  input  Swap,
  output [2:0] High,
  output [2:0] Lo
);

  Multiplexer #(.width(3), .enable("false")) multiplexer_1 (.in0(In[5:3]), .in1(In[2:0]), .out(High), .sel(Swap));
  Multiplexer #(.width(3), .enable("false")) multiplexer_2 (.in0(In[2:0]), .in1(In[5:3]), .out(Lo), .sel(Swap));

  // Notes on the sheet:
  //   Swap: pull=down
endmodule

// IB
module Instruction_Buffer (
  input  [7:0] Word_In,
  input  Reset_Data,
  input  Clock,
  input  Reset_Count,
  output [15:0] Instruction_Out,
  output [1:0] Word_Count_Out,
  output [7:0] Operand_Out
);

  wire decoder_1_out0, decoder_1_out1, decoder_1_out2, trigger_delay_1_trigger_out;

  Decoder #(.select(2), .enable("false")) decoder_1 (
    .out0(decoder_1_out0), .out1(decoder_1_out1), .out2(decoder_1_out2), .sel(Word_Count_Out));  // open: out3
  Counter #(.width(2), .max('h3)) counter_1 (
    .count(1'b1), .Q(Word_Count_Out), .clk(trigger_delay_1_trigger_out), .clr(Reset_Count));  // open: load, D, carry
  Trigger_Delay trigger_delay_1 (.Clock(Clock), .Reset(Reset_Count), .Trigger_Out(trigger_delay_1_trigger_out));
  Register #(.trigger("falling")) register_1 (
    .D(Word_In), .en(decoder_1_out0), .Q(Instruction_Out[15:8]), .clk(Clock), .clr(Reset_Data));
  Register #(.trigger("falling")) register_2 (
    .D(Word_In), .en(decoder_1_out1), .Q(Instruction_Out[7:0]), .clk(Clock), .clr(Reset_Data));
  Register #(.trigger("falling")) register_3 (
    .D(Word_In), .en(decoder_1_out2), .Q(Operand_Out), .clk(Clock), .clr(Reset_Data));
endmodule

module Bus (
);

  Multiplexer #(.select(3), .width(8), .enable("false")) multiplexer_1 ();  // open: in0, in1, in2, in3, in4, in5, in6, in7, out, sel
endmodule

// FE
module Falling_Edge (
  input  Clock,
  output Trigger
);

  wire buffer_1_out, buffer_2_out, not_1_out;

  not not_1 (not_1_out, Clock);
  buf buffer_1 (buffer_1_out, Clock);
  buf buffer_2 (buffer_2_out, buffer_1_out);
  and and_1 (Trigger, not_1_out, buffer_2_out);
endmodule

// RE
module Rising_Edge (
  input  Clock,
  output Trigger
);

  wire not_1_out;

  not not_1 (not_1_out, Clock);
  and and_1 (Trigger, not_1_out, Clock);
endmodule

// TD
module Trigger_Delay (
  input  Clock,
  input  Reset,
  output Trigger_Out
);

  wire buffer_1_out, d_ff_1_q;

  buf buffer_1 (buffer_1_out, Clock);
  D_Flip_Flop #(.trigger("falling")) d_ff_1 (
    .clk(Clock), .D(buffer_1_out), .Q(d_ff_1_q), .reset(Reset));  // open: Qn, preset, en
  and and_1 (Trigger_Out, Clock, d_ff_1_q);
endmodule
