// Logisim project Display Driver.circ as structural Verilog: 4 circuits, main circuit main
module main (
  input  in_1,
  input  Run
);

  wire _0_out, _1_out, _2_out, _3_out, _4_out, _5_out, buffer_1_out, button_1_out, button_2_out,
       button_3_out, button_4_out, button_5_out, button_6_out, cpu_1_in_port_read, falling_edge_1_trigger,
       or_1_out, or_2_out, or_3_out, priority_encoder_1_gs, Reset_out, rising_edge_1_trigger;
  wire [2:0] counter_2_q, counter_3_q, priority_encoder_1_out;
  wire [7:0] bit_extender_1_out, cpu_1_out_port, display_controller_1_out_a, display_controller_1_out_b,
       display_controller_1_out_c, display_controller_1_out_d, display_controller_1_out_e,
       display_controller_1_out_f, display_controller_1_out_g, display_controller_1_out_h,
       display_controller_2_out_a, display_controller_2_out_b, display_controller_2_out_c,
       display_controller_2_out_d, display_controller_2_out_e, display_controller_2_out_f,
       display_controller_2_out_g, display_controller_2_out_h, display_controller_3_out_a,
       display_controller_3_out_b, display_controller_3_out_c, display_controller_3_out_d,
       display_controller_3_out_e, display_controller_3_out_f, display_controller_3_out_g,
       display_controller_3_out_h;
  wire [8:8] cpu_1_out_trigger;

  Button _3 (.out(_3_out));
  Button _4 (.out(_4_out));
  Button _1 (.out(_1_out));
  Button _0 (.out(_0_out));
  Button _2 (.out(_2_out));
  Button _5 (.out(_5_out));
  Priority_Encoder priority_encoder_1 (
    .in0(_0_out), .in1(_1_out), .in2(_2_out), .in3(_3_out), .in4(_4_out), .in5(_5_out),
    .out(priority_encoder_1_out), .gs(priority_encoder_1_gs));  // open: in6, in7, en_in, en_out
  Counter counter_1 (.clk(cpu_1_in_port_read));  // open: load, D, count, Q, carry, clr
  assign bit_extender_1_out = {{5{1'b0}}, priority_encoder_1_out};  // Bit_Extender bit_extender_1
  buf buffer_1 (buffer_1_out, priority_encoder_1_gs);
  Button button_1 (.out(button_1_out));
  Button button_2 (.out(button_2_out));
  Button button_3 (.out(button_3_out));
  Button button_4 (.out(button_4_out));
  Button Reset (.out(Reset_out));
  // Probe on cpu_1_out_port[7:5]
  // Probe on cpu_1_out_port[4:2]
  CPU cpu_1 (
    .In_Port(bit_extender_1_out), .In_Port_Trigger(buffer_1_out), .In_Port_Read(cpu_1_in_port_read),
    .Reset(Reset_out), .Run(Run), .Out_Port(cpu_1_out_port), .Out_Trigger(cpu_1_out_trigger[8]));  // open: Ext_Clock, Clock_Select
  DotMatrix #(.matrixcols(8), .matrixrows(8)) dotmatrix_1 (
    .col0(display_controller_1_out_a), .col1(display_controller_1_out_b), .col2(display_controller_1_out_c),
    .col3(display_controller_1_out_d), .col4(display_controller_1_out_e), .col5(display_controller_1_out_f),
    .col6(display_controller_1_out_g), .col7(display_controller_1_out_h));
  Display_Controller display_controller_1 (
    .X_Pos(cpu_1_out_port[7:5]), .Y_Pos(cpu_1_out_port[4:2]), .Pixel(cpu_1_out_port[1]),
    .Clock(cpu_1_out_trigger[8]), .Clear(cpu_1_out_port[0]), .Out_A(display_controller_1_out_a),
    .Out_B(display_controller_1_out_b), .Out_C(display_controller_1_out_c),
    .Out_D(display_controller_1_out_d), .Out_E(display_controller_1_out_e),
    .Out_F(display_controller_1_out_f), .Out_G(display_controller_1_out_g), .Out_H(display_controller_1_out_h));
  or or_1 (or_1_out, button_2_out, button_3_out);
  or or_2 (or_2_out, button_1_out, button_4_out);
  // Probe on cpu_1_out_port
  DotMatrix #(.matrixcols(8), .matrixrows(8)) dotmatrix_2 (
    .col0(display_controller_2_out_a), .col1(display_controller_2_out_b), .col2(display_controller_2_out_c),
    .col3(display_controller_2_out_d), .col4(display_controller_2_out_e), .col5(display_controller_2_out_f),
    .col6(display_controller_2_out_g), .col7(display_controller_2_out_h));
  Display_Controller display_controller_2 (
    .X_Pos(counter_2_q), .Y_Pos(counter_3_q), .Pixel(1'b1), .Clock(falling_edge_1_trigger),
    .Clear(rising_edge_1_trigger), .Out_A(display_controller_2_out_a), .Out_B(display_controller_2_out_b),
    .Out_C(display_controller_2_out_c), .Out_D(display_controller_2_out_d),
    .Out_E(display_controller_2_out_e), .Out_F(display_controller_2_out_f),
    .Out_G(display_controller_2_out_g), .Out_H(display_controller_2_out_h));
  Counter #(.width(3), .max('h7)) counter_2 (
    .load(button_2_out), .count(or_1_out), .Q(counter_2_q), .clk(or_1_out));  // open: D, carry, clr
  or or_3 (or_3_out, or_1_out, or_2_out);
  Counter #(.width(3), .max('h7)) counter_3 (
    .load(button_1_out), .count(or_2_out), .Q(counter_3_q), .clk(or_2_out));  // open: D, carry, clr
  Rising_Edge rising_edge_1 (.Clock(or_3_out), .Trigger(rising_edge_1_trigger));
  Falling_Edge falling_edge_1 (.Clock(or_3_out), .Trigger(falling_edge_1_trigger));
  DotMatrix #(.matrixcols(8), .matrixrows(8)) dotmatrix_3 (
    .col0(display_controller_3_out_a), .col1(display_controller_3_out_b), .col2(display_controller_3_out_c),
    .col3(display_controller_3_out_d), .col4(display_controller_3_out_e), .col5(display_controller_3_out_f),
    .col6(display_controller_3_out_g), .col7(display_controller_3_out_h));
  Display_Controller display_controller_3 (
    .X_Pos(counter_2_q), .Y_Pos(counter_3_q), .Pixel(in_1), .Clock(button_5_out), .Clear(button_6_out),
    .Out_A(display_controller_3_out_a), .Out_B(display_controller_3_out_b),
    .Out_C(display_controller_3_out_c), .Out_D(display_controller_3_out_d),
    .Out_E(display_controller_3_out_e), .Out_F(display_controller_3_out_f),
    .Out_G(display_controller_3_out_g), .Out_H(display_controller_3_out_h));
  Button button_5 (.out(button_5_out));
  Button button_6 (.out(button_6_out));
endmodule

// DC
module Display_Controller (
  input  [2:0] X_Pos,
  input  [2:0] Y_Pos,
  input  Pixel,
  input  Clock,
  input  Clear,
  output [7:0] Out_A,
  output [7:0] Out_B,
  output [7:0] Out_C,
  output [7:0] Out_D,
  output [7:0] Out_E,
  output [7:0] Out_F,
  output [7:0] Out_G,
  output [7:0] Out_H
);

  wire decoder_1_out0, decoder_1_out1, decoder_1_out2, decoder_1_out3, decoder_1_out4, decoder_1_out5,
       decoder_1_out6, decoder_1_out7;

  Decoder #(.select(3), .enable("false")) decoder_1 (
    .out0(decoder_1_out0), .out1(decoder_1_out1), .out2(decoder_1_out2), .out3(decoder_1_out3),
    .out4(decoder_1_out4), .out5(decoder_1_out5), .out6(decoder_1_out6), .out7(decoder_1_out7), .sel(X_Pos));
  Smart_Buffer smart_buffer_1 (
    .Bit_Select(Y_Pos), .Bit_Status(Pixel), .CS(decoder_1_out0), .Clock(Clock), .Q(Out_A), .Clear(Clear));
  Smart_Buffer smart_buffer_2 (
    .Bit_Select(Y_Pos), .Bit_Status(Pixel), .CS(decoder_1_out1), .Clock(Clock), .Q(Out_B), .Clear(Clear));
  Smart_Buffer smart_buffer_3 (
    .Bit_Select(Y_Pos), .Bit_Status(Pixel), .CS(decoder_1_out2), .Clock(Clock), .Q(Out_C), .Clear(Clear));
  Smart_Buffer smart_buffer_4 (
    .Bit_Select(Y_Pos), .Bit_Status(Pixel), .CS(decoder_1_out3), .Clock(Clock), .Q(Out_D), .Clear(Clear));
  Smart_Buffer smart_buffer_5 (
    .Bit_Select(Y_Pos), .Bit_Status(Pixel), .CS(decoder_1_out4), .Clock(Clock), .Q(Out_E), .Clear(Clear));
  Smart_Buffer smart_buffer_6 (
    .Bit_Select(Y_Pos), .Bit_Status(Pixel), .CS(decoder_1_out5), .Clock(Clock), .Q(Out_F), .Clear(Clear));
  Smart_Buffer smart_buffer_7 (
    .Bit_Select(Y_Pos), .Bit_Status(Pixel), .CS(decoder_1_out6), .Clock(Clock), .Q(Out_G), .Clear(Clear));
  Smart_Buffer smart_buffer_8 (
    .Bit_Select(Y_Pos), .Bit_Status(Pixel), .CS(decoder_1_out7), .Clock(Clock), .Q(Out_H), .Clear(Clear));
endmodule

// SB
module Smart_Buffer (
  input  [2:0] Bit_Select,
  input  Bit_Status,
  input  Clear,
  input  CS,
  input  Clock,
  output [7:0] Q
);

  wire buffer_1_out, buffer_2_out, buffer_3_out, buffer_4_out, buffer_5_out;
  wire [7:0] and_1_out, decoder_1_out7, decoder_2_out7, multiplexer_1_out, not_1_out, or_1_out;

  Decoder #(.select(3), .enable("false")) decoder_1 (
    .out0(decoder_1_out7[7]), .out1(decoder_1_out7[6]), .out2(decoder_1_out7[5]), .out3(decoder_1_out7[4]),
    .out4(decoder_1_out7[3]), .out5(decoder_1_out7[2]), .out6(decoder_1_out7[1]), .out7(decoder_1_out7[0]),
    .sel(Bit_Select));
  assign not_1_out = ~decoder_1_out7;  // NOT_Gate not_1, 8 bits wide
  Decoder #(.select(3), .enable("false")) decoder_2 (
    .out0(decoder_2_out7[7]), .out1(decoder_2_out7[6]), .out2(decoder_2_out7[5]), .out3(decoder_2_out7[4]),
    .out4(decoder_2_out7[3]), .out5(decoder_2_out7[2]), .out6(decoder_2_out7[1]), .out7(decoder_2_out7[0]),
    .sel(Bit_Select));
  assign and_1_out = not_1_out & Q;  // AND_Gate and_1, 8 bits wide
  Multiplexer #(.width(8), .enable("false")) multiplexer_1 (
    .in0(and_1_out), .in1(or_1_out), .out(multiplexer_1_out), .sel(Bit_Status));
  assign or_1_out = decoder_2_out7 | Q;  // OR_Gate or_1, 8 bits wide
  Register #(.trigger("falling")) register_1 (.D(multiplexer_1_out), .en(CS), .Q(Q), .clk(buffer_1_out), .clr(Clear));
  buf buffer_1 (buffer_1_out, buffer_2_out);
  buf buffer_2 (buffer_2_out, buffer_3_out);
  buf buffer_3 (buffer_3_out, buffer_4_out);
  buf buffer_4 (buffer_4_out, buffer_5_out);
  buf buffer_5 (buffer_5_out, Clock);
endmodule

// IQ
module Input_Queue (
  input  Write,
  input  [2:0] Value,
  input  Read,
  output [2:0] Out
);

  wire and_1_out, or_1_out, or_2_out, rising_edge_1_trigger, trigger_delay_1_trigger_out;
  wire [2:0] counter_1_q, shift_register_1_q0, shift_register_1_q1, shift_register_1_q2, shift_register_1_q3,
       shift_register_1_q4, shift_register_1_q5, shift_register_1_q6, shift_register_1_q7;

  buf and_1 (and_1_out, Read);  // AND_Gate
  Trigger_Delay trigger_delay_1 (.Clock(Write), .Reset(and_1_out), .Trigger_Out(trigger_delay_1_trigger_out));
  Rising_Edge rising_edge_1 (.Clock(Read), .Trigger(rising_edge_1_trigger));
  Shift_Register #(.width(3)) shift_register_1 (
    .in(Value), .clk(Write), .q0(shift_register_1_q0), .q1(shift_register_1_q1), .q2(shift_register_1_q2),
    .q3(shift_register_1_q3), .q4(shift_register_1_q4), .q5(shift_register_1_q5), .q6(shift_register_1_q6),
    .q7(shift_register_1_q7));  // open: shift, out, load, clr, d0, d1, d2, d3, d4, d5, d6, d7
  Counter #(.width(3), .max('h7), .ongoal("stay")) counter_1 (
    .load(Read), .count(or_1_out), .Q(counter_1_q), .clk(or_2_out));  // open: D, carry, clr
  or or_1 (or_1_out, Write, Read);
  or or_2 (or_2_out, trigger_delay_1_trigger_out, rising_edge_1_trigger);
  Multiplexer #(.select(3), .width(3), .enable("false")) multiplexer_1 (
    .in0(shift_register_1_q0), .in1(shift_register_1_q1), .in2(shift_register_1_q2),
    .in3(shift_register_1_q3), .in4(shift_register_1_q4), .in5(shift_register_1_q5),
    .in6(shift_register_1_q6), .in7(shift_register_1_q7), .out(Out), .sel(counter_1_q));
endmodule
