// Logisim project JCPU.circ as structural Verilog: 6 circuits, main circuit main
module main (
);

  wire branch_1_jmp_2, clock_1_execute_2, clock_1_fetch, control_1_acc, control_1_execute, control_1_out,
       decoder_1_out0, decoder_1_out1, decoder_1_out2, decoder_1_out3, decoder_2_out0, decoder_2_out1,
       decoder_2_out2, not_1_out, or_1_out;
  wire [1:0] control_1_addr_bus, control_1_alu, control_1_data_bus, control_1_ib, control_1_pc, control_1_ram;
  wire [7:0] Acc_q, buffer_1_out, controlled_buffer_1_out, controlled_buffer_2_out, controlled_buffer_6_out,
       instruction_buffer_1_inst, instruction_buffer_1_lit, Out_q, PC_q;

  Clock clock_1 (.Execute(control_1_execute), .Fetch(clock_1_fetch), .Execute_2(clock_1_execute_2));
  Decoder #(.select(2), .enable("false")) decoder_1 (
    .out0(decoder_1_out0), .out1(decoder_1_out1), .out2(decoder_1_out2), .out3(decoder_1_out3),
    .sel(control_1_data_bus));
  Decoder #(.select(2), .enable("false")) decoder_2 (
    .out0(decoder_2_out0), .out1(decoder_2_out1), .out2(decoder_2_out2), .sel(control_1_addr_bus));  // open: out3
  assign buffer_1_out = controlled_buffer_1_out;  // Buffer buffer_1, 8 bits wide
  assign controlled_buffer_1_out = decoder_1_out0 ? Acc_q : 8'bz;  // Controlled_Buffer controlled_buffer_1
  Register Acc (.D(buffer_1_out), .en(control_1_acc), .Q(Acc_q), .clk(clock_1_execute_2));  // open: clr
  assign controlled_buffer_2_out = decoder_2_out0 ? Acc_q : 8'bz;  // Controlled_Buffer controlled_buffer_2
  ALU alu_1 (.In_A(Acc_q), .In_B(controlled_buffer_1_out), .Op(control_1_alu), .Out(buffer_1_out));
  Branch branch_1 (.Acc(Acc_q), .jz(control_1_pc[1]), .jmp(control_1_pc[0]), .Jmp_2(branch_1_jmp_2));
  Counter PC (.load(branch_1_jmp_2), .D(controlled_buffer_1_out), .Q(PC_q), .clk(or_1_out));  // open: count, carry, clr
  or or_1 (or_1_out, clock_1_fetch, clock_1_execute_2);
  Control control_1 (
    .Execute(control_1_execute), .Instruction(instruction_buffer_1_inst), .Data_Bus(control_1_data_bus),
    .Addr_Bus(control_1_addr_bus), .Acc(control_1_acc), .ALU(control_1_alu), .PC(control_1_pc),
    .RAM(control_1_ram), .IB(control_1_ib), .Out(control_1_out));
  assign controlled_buffer_1_out = decoder_1_out1 ? PC_q : 8'bz;  // Controlled_Buffer controlled_buffer_3
  assign controlled_buffer_2_out = decoder_2_out1 ? PC_q : 8'bz;  // Controlled_Buffer controlled_buffer_4
  assign controlled_buffer_1_out = decoder_1_out2 ? controlled_buffer_6_out : 8'bz;  // Controlled_Buffer controlled_buffer_5
  assign controlled_buffer_6_out = not_1_out ? controlled_buffer_1_out : 8'bz;  // Controlled_Buffer controlled_buffer_6
  RAM ram_1 (
    .addr(controlled_buffer_2_out), .data(controlled_buffer_6_out), .sel(control_1_ram[1]),
    .clk(clock_1_execute_2), .ld(control_1_ram[0]));  // open: clr
  not not_1 (not_1_out, control_1_ram[0]);
  assign controlled_buffer_1_out = decoder_1_out3 ? instruction_buffer_1_lit : 8'bz;  // Controlled_Buffer controlled_buffer_7
  Instruction_Buffer instruction_buffer_1 (
    .RAM(controlled_buffer_1_out), .Rst(control_1_ib[1]), .Clk(control_1_ib[0]),
    .Inst(instruction_buffer_1_inst), .Lit(instruction_buffer_1_lit));
  assign controlled_buffer_2_out = decoder_2_out2 ? instruction_buffer_1_lit : 8'bz;  // Controlled_Buffer controlled_buffer_8
  Register Out (.D(controlled_buffer_1_out), .en(control_1_out), .Q(Out_q), .clk(clock_1_execute_2));  // open: clr
  Hex_Digit_Display hex_digit_display_1 (.value(Out_q[7:4]));  // open: dp
  Hex_Digit_Display hex_digit_display_2 (.value(Out_q[3:0]));  // open: dp
endmodule

module ALU (
  input  [7:0] In_A,
  input  [7:0] In_B,
  input  [1:0] Op,
  output [7:0] Out
);

  wire [7:0] adder_1_out, not_1_out, or_1_out;

  Adder adder_1 (.a(In_A), .b(In_B), .out(adder_1_out));  // open: cin, cout
  assign or_1_out = In_A | In_B;  // OR_Gate or_1, 8 bits wide
  assign not_1_out = ~In_A;  // NOT_Gate not_1, 8 bits wide
  Multiplexer #(.select(2), .width(8), .enable("false")) multiplexer_1 (
    .in1(adder_1_out), .in2(or_1_out), .in3(not_1_out), .out(Out), .sel(Op));  // open: in0
endmodule

// IB
module Instruction_Buffer (
  input  [7:0] RAM,
  input  Rst,
  input  Clk,
  output [7:0] Inst,
  output [7:0] Lit
);

  wire buffer_1_out, decoder_1_out0, decoder_1_out1, t_ff_1_q;

  Decoder #(.enable("false")) decoder_1 (.out0(decoder_1_out0), .out1(decoder_1_out1), .sel(t_ff_1_q));
  T_Flip_Flop t_ff_1 (.clk(Clk), .T(1'b1), .Q(t_ff_1_q), .preset(Rst));  // open: Qn, reset, en
  Register Instruction (.D(RAM), .en(decoder_1_out0), .Q(Inst), .clk(buffer_1_out));  // open: clr
  Register Literal (.D(RAM), .en(decoder_1_out1), .Q(Lit), .clk(buffer_1_out));  // open: clr
  buf buffer_1 (buffer_1_out, Clk);
endmodule

// CTRL
module Control (
  input  [7:0] Instruction,
  output Execute,
  output [1:0] Data_Bus,
  output [1:0] Addr_Bus,
  output Acc,
  output [1:0] ALU,
  output [1:0] PC,
  output [1:0] RAM,
  output [1:0] IB,
  output Out
);

  wire mov;
  wire [7:0] not_1_out;

  assign not_1_out = ~Instruction;  // NOT_Gate not_1, 8 bits wide
  and and_1 (mov, not_1_out[1], not_1_out[0]);
  and and_2 (Execute, Instruction[2], Instruction[3]);

  assign ALU = Instruction[1:0];

  // Other names for the same wires on the sheet: Addr_Bus_t[1:0] = Instruction[7:6];
  //   Data_Bus_t[1:0] = Instruction[3:2]
endmodule

// BRA
module Branch (
  input  [7:0] Acc,
  input  jz,
  input  jmp,
  output Jmp_2
);

  wire and_1_out, comparator_1_eq;

  Comparator comparator_1 (.a(Acc), .b({8{1'b0}}), .eq(comparator_1_eq));  // open: gt, lt
  and and_1 (and_1_out, comparator_1_eq, jz);
  or or_1 (Jmp_2, and_1_out, jmp);
endmodule

module Clock (
  input  Execute,
  output Fetch,
  output Execute_2
);

  wire clock_1_out, t_ff_1_qn;

  Clock_part clock_1 (.out(clock_1_out));
  T_Flip_Flop t_ff_1 (.clk(clock_1_out), .T(1'b1), .Q(Fetch), .Qn(t_ff_1_qn));  // open: preset, reset, en
  and and_1 (Execute_2, t_ff_1_qn, Execute);
endmodule
