// Logisim project TTY with CPU3.circ as structural Verilog: 1 circuit, main circuit main
module main (
  input  Run
);

  wire cpu_1_p4, Reset_out;
  wire [3:0] button_3_out;
  wire [6:0] bitselector_1_out;
  wire [7:0] cpu_1_p3;

  Button Reset (.out(Reset_out));
  // CPU cpu_1: pin names not known; wires that end beside it: Run, Reset_out, cpu_1_p3, cpu_1_p4
  BitSelector #(.group(7)) bitselector_1 (.in(cpu_1_p3), .out(bitselector_1_out), .sel(1'b0));
  TTY tty_1 (.data(bitselector_1_out), .clk(cpu_1_p4), .clr(Reset_out));  // open: we
  Button button_1 (.out(button_3_out[3]));
  Button button_2 (.out(button_3_out[1]));
  Button button_3 (.out(button_3_out[0]));
  Button button_4 (.out(button_3_out[2]));
endmodule
