// Logisim project disp.circ as structural Verilog: 1 circuit, main circuit main
// Ax
module main (
  input  [7:0] in_1,
  input  in_2
);

  wire undriven, undriven_2, undriven_3, undriven_4, undriven_5, undriven_6, undriven_7, undriven_8,
       undriven_9;
  wire [7:0] ram_1_data, register_1_q, register_2_q, register_3_q, register_4_q, register_5_q, register_6_q,
       register_7_q, register_8_q;

  Controlled_Buffer #(.width(8)) controlled_buffer_1 (.in(in_1), .en(in_2));  // open: out
  RAM #(.addrWidth(3)) ram_1 (.data(ram_1_data));  // open: addr, sel, clk, ld, clr
  Register register_1 (.D(ram_1_data), .en(undriven), .Q(register_1_q), .clk(undriven_9));  // open: clr
  Register register_2 (.D(ram_1_data), .en(undriven_2), .Q(register_2_q), .clk(undriven_9));  // open: clr
  Register register_3 (.D(ram_1_data), .en(undriven_3), .Q(register_3_q), .clk(undriven_9));  // open: clr
  Register register_4 (.D(ram_1_data), .en(undriven_4), .Q(register_4_q), .clk(undriven_9));  // open: clr
  Register register_5 (.D(ram_1_data), .en(undriven_5), .Q(register_5_q), .clk(undriven_9));  // open: clr
  Register register_6 (.D(ram_1_data), .en(undriven_6), .Q(register_6_q), .clk(undriven_9));  // open: clr
  Register register_7 (.D(ram_1_data), .en(undriven_7), .Q(register_7_q), .clk(undriven_9));  // open: clr
  Register register_8 (.D(ram_1_data), .en(undriven_8), .Q(register_8_q), .clk(undriven_9));  // open: clr
  Register #(.width(32)) register_9 ();  // open: D, en, Q, clk, clr
  Register #(.width(32)) register_10 ();  // open: D, en, Q, clk, clr
  DotMatrix #(.matrixcols(8), .matrixrows(8)) dotmatrix_1 ();  // open: col0, col1, col2, col3, col4, col5, col6, col7
endmodule
