// Logisim project terminal.circ as structural Verilog: 1 circuit, main circuit main
module main (
  input  Run,
  input  Pause
);

  wire cpu_1_in_port_read, cpu_1_out_trigger, keyboard_1_avail, Reset_out, Step_out;
  wire [6:0] bit_extender_2_out, keyboard_1_data;
  wire [7:0] bit_extender_1_out, cpu_1_out_port;

  Keyboard keyboard_1 (
    .clk(cpu_1_in_port_read), .clr(Reset_out), .avail(keyboard_1_avail), .data(keyboard_1_data));  // open: re
  Button Reset (.out(Reset_out));
  assign bit_extender_1_out = {{1{1'b0}}, keyboard_1_data};  // Bit_Extender bit_extender_1
  Button Step (.out(Step_out));
  CPU cpu_1 (
    .In_Port(bit_extender_1_out), .In_Port_Trigger(keyboard_1_avail), .In_Port_Read(cpu_1_in_port_read),
    .Reset(Reset_out), .Run(Run), .Ext_Clock(Step_out), .Clock_Select(Pause), .Out_Port(cpu_1_out_port),
    .Out_Trigger(cpu_1_out_trigger));
  Bit_Extender #(.out_width(7)) bit_extender_2 (.in(cpu_1_out_port), .out(bit_extender_2_out));
  TTY tty_1 (.data(bit_extender_2_out), .clk(cpu_1_out_trigger), .clr(Reset_out));  // open: we
endmodule
